// Logisim project 16bitCPU.circ as structural Verilog
module project_ao (
  input  [15:0] A,
  input  [15:0] B,
  input  [3:0] selectors,
  output [15:0] out_4
);

  wire [15:0] adder_1_out, and_1_out, divider_1_out, divider_1_rem, multiplier_1_out, negator_1_out,
       negator_2_out, or_1_out, shifter_1_out, shifter_2_out, shifter_3_out, shifter_4_out, subtractor_1_out,
       xor_1_out;

  Adder #(.width(16)) adder_1 (.a(A), .b(B), .out(adder_1_out));  // open: cin, cout
  assign and_1_out = A & B;  // AND_Gate and_1, 16 bits wide
  assign or_1_out = A | B;  // OR_Gate or_1, 16 bits wide
  assign xor_1_out = A ^ B;  // XOR_Gate xor_1, 16 bits wide
  Divider #(.width(16)) divider_1 (.a(A), .b(B), .out(divider_1_out), .rem(divider_1_rem));  // open: upper
  Multiplier #(.width(16)) multiplier_1 (.a(A), .b(B), .out(multiplier_1_out));  // open: cin, cout
  Subtractor #(.width(16)) subtractor_1 (.a(A), .b(B), .out(subtractor_1_out));  // open: bin, bout
  Shifter #(.width(16)) shifter_1 (.in(A), .\dist (4'b0010), .out(shifter_1_out));
  Shifter #(.width(16)) shifter_2 (.in(B), .\dist (4'b0010), .out(shifter_2_out));
  Shifter #(.shift("lr"), .width(16)) shifter_3 (.in(A), .\dist (4'b0010), .out(shifter_3_out));
  Shifter #(.width(16)) shifter_4 (.in(B), .\dist (4'b0010), .out(shifter_4_out));
  Negator #(.width(16)) negator_1 (.in(A), .out(negator_1_out));
  Negator #(.width(16)) negator_2 (.in(B), .out(negator_2_out));
  Multiplexer #(.select(4), .width(16)) multiplexer_1 (
    .in0(adder_1_out), .in1(and_1_out), .in2(or_1_out), .in3(xor_1_out), .in4(divider_1_out),
    .in5(divider_1_rem), .in6(multiplier_1_out), .in7(subtractor_1_out), .in8(shifter_1_out),
    .in9(shifter_2_out), .in10(shifter_3_out), .in11(shifter_4_out), .in12(negator_1_out),
    .in13(negator_2_out), .out(out_4), .sel(selectors));  // open: in14, in15

  // Notes on the sheet:
  //   Arithmetic Unit
  //   au_output
endmodule

module project_ro (
  input  [15:0] A,
  input  [15:0] B,
  input  [2:0] selectors,
  output lu_output
);

  wire comparator_1_eq, comparator_1_gt, comparator_1_lt, not_1_out, or_1_out, or_2_out;

  Comparator #(.mode("unsigned"), .width(16)) comparator_1 (
    .a(A), .b(B), .gt(comparator_1_gt), .eq(comparator_1_eq), .lt(comparator_1_lt));
  or or_1 (or_1_out, comparator_1_gt, comparator_1_eq);
  or or_2 (or_2_out, comparator_1_lt, comparator_1_eq);
  not not_1 (not_1_out, comparator_1_eq);
  Multiplexer #(.select(3)) multiplexer_1 (
    .in0(comparator_1_gt), .in1(comparator_1_eq), .in2(or_1_out), .in3(comparator_1_lt), .in4(or_2_out),
    .in5(not_1_out), .out(lu_output), .sel(selectors));  // open: in6, in7

  // Notes on the sheet:
  //   comparator
  //   Logic Unit
  //   >
  //   =
  //   >=
  //   <
  //   <=
  //   !=
endmodule

module project_alu (
  input  [15:0] A,
  input  OE,
  input  [3:0] in_3,
  input  [15:0] B,
  input  [2:0] selectors,
  output [15:0] AUDout,
  output [15:0] AUResult,
  output out_8
);

  project_ao AU (.B(B), .A(A), .selectors(in_3), .out_4(AUResult));
  project_ro LU (.A(A), .B(B), .selectors(selectors), .lu_output(out_8));
  assign AUDout = OE ? AUResult : 16'bz;  // Controlled_Buffer controlled_buffer_1

  // Notes on the sheet:
  //   Arithmetic Logic Unit
  //   selectors
endmodule

module project_cpu (
  input  [15:0] Test_Data,
  input  Test_OE,
  input  OE_MAR,
  input  WE_MAR,
  input  Reset_MAR,
  input  IR_OE,
  input  WE,
  input  Reset,
  input  OE_MBR,
  input  WE_MBR,
  input  OE_Dout_MBR,
  input  Reset_MBR,
  input  WE_A,
  input  Reset_A,
  input  OE_ALU,
  input  [2:0] in_16,
  input  OE_Output,
  input  [3:0] in_18,
  input  WE_Output,
  input  WE_B,
  input  Reset_B,
  output [7:0] MAR_Content,
  output [15:0] Result,
  output [15:0] out_24,
  output out_25,
  output [15:0] Output_Content
);

  wire clock_1_out;
  wire [7:0] bitselector_1_out, controlled_buffer_4_out;
  wire [15:0] controlled_buffer_1_out, MBR_q, project_alu_1_audout, Register_A_q, Register_B_q;

  Clock clock_1 (.out(clock_1_out));
  Register #(.width(16)) Instruction_Register (
    .D(project_alu_1_audout), .en(WE), .clk(clock_1_out), .Q(Result), .clr(Reset));
  assign controlled_buffer_1_out = IR_OE ? Result : 16'bz;  // Controlled_Buffer controlled_buffer_1
  BitSelector #(.group(8), .width(16)) bitselector_1 (
    .in(controlled_buffer_1_out), .out(bitselector_1_out), .sel(1'b1));
  Register #(.width(16)) Register_A (
    .D(project_alu_1_audout), .en(WE_A), .clk(clock_1_out), .Q(Register_A_q), .clr(Reset_A));
  Register #(.width(16)) Register_B (
    .D(project_alu_1_audout), .en(WE_B), .clk(clock_1_out), .Q(Register_B_q), .clr(Reset_B));
  project_alu project_alu_1 (
    .A(Register_A_q), .B(Register_B_q), .in_3(in_18), .selectors(in_16), .OE(OE_ALU), .out_8(out_25),
    .AUDout(project_alu_1_audout), .AUResult(out_24));
  LED led_1 (.in(project_alu_1_audout[15]));
  LED led_2 (.in(project_alu_1_audout[14]));
  LED led_3 (.in(project_alu_1_audout[13]));
  LED led_4 (.in(project_alu_1_audout[12]));
  LED led_5 (.in(project_alu_1_audout[11]));
  assign project_alu_1_audout = Test_OE ? Test_Data : 16'bz;  // Controlled_Buffer controlled_buffer_2
  LED led_6 (.in(project_alu_1_audout[10]));
  LED led_7 (.in(project_alu_1_audout[9]));
  LED led_8 (.in(project_alu_1_audout[8]));
  LED led_9 (.in(project_alu_1_audout[7]));
  LED led_10 (.in(project_alu_1_audout[6]));
  LED led_11 (.in(project_alu_1_audout[5]));
  LED led_12 (.in(project_alu_1_audout[4]));
  LED led_13 (.in(project_alu_1_audout[3]));
  LED led_14 (.in(project_alu_1_audout[2]));
  LED led_15 (.in(project_alu_1_audout[1]));
  LED led_16 (.in(project_alu_1_audout[0]));
  Register #(.width(16)) Output_Register (
    .D(project_alu_1_audout), .en(WE_Output), .clk(clock_1_out), .Q(Output_Content));  // open: clr
  Register MAR (.D(bitselector_1_out), .en(WE_MAR), .clk(clock_1_out), .Q(MAR_Content), .clr(Reset_MAR));
  Register #(.width(16)) MBR (.D(project_alu_1_audout), .en(WE_MBR), .clk(clock_1_out), .Q(MBR_q), .clr(Reset_MBR));
  assign project_alu_1_audout = OE_Output ? Output_Content : 16'bz;  // Controlled_Buffer controlled_buffer_3
  assign controlled_buffer_4_out = OE_MAR ? MAR_Content : 8'bz;  // Controlled_Buffer controlled_buffer_4
  assign project_alu_1_audout = OE_MBR ? MBR_q : 16'bz;  // Controlled_Buffer controlled_buffer_5
  assign project_alu_1_audout = OE_Dout_MBR ? MBR_q : 16'bz;  // Controlled_Buffer controlled_buffer_6
  LED led_17 (.in(project_alu_1_audout[15]));
  LED led_18 (.in(project_alu_1_audout[14]));
  LED led_19 (.in(project_alu_1_audout[13]));
  LED led_20 (.in(project_alu_1_audout[12]));
  LED led_21 (.in(project_alu_1_audout[11]));
  LED led_22 (.in(project_alu_1_audout[10]));
  LED led_23 (.in(project_alu_1_audout[9]));
  LED led_24 (.in(project_alu_1_audout[8]));
  LED led_25 (.in(project_alu_1_audout[7]));
  LED led_26 (.in(project_alu_1_audout[6]));
  LED led_27 (.in(project_alu_1_audout[5]));
  LED led_28 (.in(project_alu_1_audout[4]));
  LED led_29 (.in(project_alu_1_audout[3]));
  LED led_30 (.in(project_alu_1_audout[2]));
  LED led_31 (.in(project_alu_1_audout[1]));
  LED led_32 (.in(project_alu_1_audout[0]));
endmodule
