// Logisim project 8_bit_register_circuit.circ as structural Verilog: 1 circuit, main circuit main
module main (
  input  [7:0] Din,
  input  we,
  input  clk,
  input  reset,
  output [7:0] Dout
);

  Register register_1 (.D(Din), .en(we), .clk(clk), .Q(Dout), .clr(reset));

  // Notes on the sheet:
  //   8 bit register
endmodule
